# Fritzing sketch AC_Ampere_Hour_Meter (saved by Fritzing 0.8.7b)
circuit board: 17.6106cm x 9.99066cm
breadboards: 1

parts:
  U1 = LCD-16X2 [package=lcd-16x2]
  S1 = Toggle Switch [package=THT]
  S2 = Square Pushbutton
  Part2 = ACS712 Low Current Sensor Board v12
  Part3 = ACS712 Low Current Sensor Board v12
  VCC1 = Battery block 9V
  Part1 = Arduino Pro Mini v13
  U2 = POT_SWITCH [package=pot_pth]
  R1 = Resistor [tolerance=±5% resistance=1k package=THT]
  R2 = Resistor [tolerance=±5% resistance=1k package=THT]
  R3 = Resistor [tolerance=±5% resistance=1k package=THT]

nets:
  GND: U1.VSS, U1.R_W, U1.A, Part2.GND, Part3.GND, VCC1.-, U2.G$1_E, R1.Pin_1, R2.Pin_1, R3.Pin_1
  5V: U1.VDD, U1.K, S1.COM, S2.leg1, Part2.5V, Part3.5V, Part1.VCC, U2.G$1_A
  N1: U1.VO, U2.G$2_1
  N2: U1.RS, Part1.D2
  N3: U1.E, Part1.D3_PWM
  N4: U1.DB4, Part1.D4
  N5: U1.DB5, Part1.D5_PWM
  N6: U1.DB6, Part1.D6_PWM
  N7: U1.DB7, Part1.D7
  N8: S2.leg0, Part1.D8
  N9: Part2.IP+, Part3.IP-
  N10: Part2.VO, Part1.A1, Part1.D11_PWM/MOSI, R3.Pin_0
  N11: Part3.VO, Part1.A0, Part1.D10_PWM/SS, R1.Pin_0
  N12: VCC1.+, Part1.RAW
