# Fritzing sketch Analog_Joystick (saved by Fritzing 0.8.7b)
circuit board: 9.38892cm x 11.012cm
breadboards: 1

parts:
  J2 = female pin header, 3 pins [form="♀ (female)"]
  J3 = female pin header, 3 pins [form="♀ (female)"]
  J4 = female pin header, 4 pins [form="♀ (female)"]
  J5 = female pin header, 4 pins [form="♀ (female)"]
  J6 = female pin header, 3 pins [form="♀ (female)"]
  J7 = female pin header, 3 pins [form="♀ (female)"]
  J8 = female pin header, 4 pins [form="♀ (female)"]
  J9 = female pin header, 3 pins [form="♀ (female)"]
  J10 = female pin header, 3 pins [form="♀ (female)"]
  J11 = female pin header, 4 pins [form="♀ (female)"]
  J12 = female pin header, 3 pins [form="♀ (female)"]
  J13 = female pin header, 3 pins [form="♀ (female)"]

nets:
  N1: J2.pin1, J3.pin3, J4.pin1
  N2: J2.pin2, J4.pin2
  N3: J2.pin3, J3.pin1, J4.pin3
  N4: J3.pin2, J4.pin4
  N5: J5.pin1, J6.pin1, J7.pin3
  N6: J5.pin2, J6.pin2
  N7: J5.pin3, J6.pin3, J7.pin1
  N8: J5.pin4, J7.pin2
  N9: J8.pin1, J9.pin1, J10.pin3
  N10: J8.pin2, J9.pin2
  N11: J8.pin3, J9.pin3, J10.pin1
  N12: J8.pin4, J10.pin2
  N13: J11.pin1, J12.pin3, J13.pin1
  N14: J11.pin2, J13.pin2
  N15: J11.pin3, J12.pin1, J13.pin3
  N16: J11.pin4, J12.pin2
