# Fritzing sketch BO_MotorPair_L293N (saved by Fritzing 0.8.3b)
breadboards: 1

parts:
  L293N1 = L293N
  VCC1 = Battery block 9V
  IC1 = Voltage Regulator [package=to-220-alt]
  M1 = DC Motor
  Part1 = Arduino Uno (Rev3)
  M2 = DC Motor

nets:
  N1: L293N1.C2, M1.pin_2
  N2: L293N1.C3, M1.pin_1
  N3: L293N1.C4, VCC1.+, IC1.IN
  N4: L293N1.C5, Part1.D2
  N5: L293N1.C6, Part1.D3_PWM
  N6: L293N1.C7, Part1.D4
  GND: L293N1.C8, VCC1.-, IC1.GND, Part1.GND, Part1.VIN
  N7: L293N1.C9, IC1.OUT
  N8: L293N1.C10, Part1.D8
  N9: L293N1.C11, Part1.D9_PWM
  N10: L293N1.C12, Part1.D7
  N11: L293N1.C13, M2.pin_2
  N12: L293N1.C14, M2.pin_1
