# Fritzing sketch ERP_10ServoController (saved by Fritzing 0.8.7b)
circuit board: 17.4413cm x 12.8129cm
breadboards: 1

parts:
  J5 = female pin header, 3 pins [form="♀ (female)"]
  J6 = female pin header, 3 pins [form="♀ (female)"]
  J7 = female pin header, 3 pins [form="♀ (female)"]
  J8 = female pin header, 3 pins [form="♀ (female)"]
  J9 = female pin header, 3 pins [form="♀ (female)"]
  J10 = female pin header, 3 pins [form="♀ (female)"]
  J11 = female pin header, 3 pins [form="♀ (female)"]
  J12 = female pin header, 3 pins [form="♀ (female)"]
  J13 = female pin header, 3 pins [form="♀ (female)"]
  J14 = female pin header, 3 pins [form="♀ (female)"]
  J15 = female pin header, 3 pins [form="♀ (female)"]
  J16 = female pin header, 12 pins [form="♀ (female)"]
  J17 = female pin header, 3 pins [form="♀ (female)"]
  J18 = Power Jack [package=power_jack_pth_lock]
  J19 = female pin header, 3 pins [form="♀ (female)"]
  J20 = female pin header, 3 pins [form="♀ (female)"]
  J21 = female pin header, 3 pins [form="♀ (female)"]
  J22 = female pin header, 3 pins [form="♀ (female)"]
  J23 = female pin header, 3 pins [form="♀ (female)"]
  J24 = female pin header, 12 pins [form="♀ (female)"]
  J25 = female pin header, 3 pins [form="♀ (female)"]
  J26 = female pin header, 3 pins [form="♀ (female)"]
  J27 = female pin header, 3 pins [form="♀ (female)"]
  J28 = female pin header, 3 pins [form="♀ (female)"]
  J29 = female pin header, 3 pins [form="♀ (female)"]
  J30 = female pin header, 3 pins [form="♀ (female)"]
  J31 = female pin header, 3 pins [form="♀ (female)"]
  J32 = Power Jack [package=power_jack_pth_lock]
  J33 = female pin header, 3 pins [form="♀ (female)"]
  J34 = female pin header, 3 pins [form="♀ (female)"]
  J35 = female pin header, 3 pins [form="♀ (female)"]
  J36 = female pin header, 3 pins [form="♀ (female)"]
  J37 = female pin header, 3 pins [form="♀ (female)"]
  J38 = female pin header, 12 pins [form="♀ (female)"]
  J39 = female pin header, 3 pins [form="♀ (female)"]
  J40 = female pin header, 3 pins [form="♀ (female)"]
  J41 = female pin header, 3 pins [form="♀ (female)"]
  J42 = female pin header, 3 pins [form="♀ (female)"]
  J43 = female pin header, 3 pins [form="♀ (female)"]
  J44 = female pin header, 3 pins [form="♀ (female)"]
  J45 = female pin header, 3 pins [form="♀ (female)"]
  J46 = Power Jack [package=power_jack_pth_lock]
  J47 = female pin header, 3 pins [form="♀ (female)"]
  J48 = female pin header, 3 pins [form="♀ (female)"]
  J49 = female pin header, 3 pins [form="♀ (female)"]
  J50 = female pin header, 3 pins [form="♀ (female)"]
  J51 = female pin header, 3 pins [form="♀ (female)"]
  J52 = female pin header, 12 pins [form="♀ (female)"]
  J53 = female pin header, 3 pins [form="♀ (female)"]
  J54 = female pin header, 3 pins [form="♀ (female)"]
  J55 = female pin header, 3 pins [form="♀ (female)"]
  J56 = female pin header, 3 pins [form="♀ (female)"]
  J57 = female pin header, 3 pins [form="♀ (female)"]
  J58 = female pin header, 3 pins [form="♀ (female)"]
  J59 = female pin header, 3 pins [form="♀ (female)"]
  J60 = Power Jack [package=power_jack_pth_lock]

nets:
  N1: J5.pin1, J6.pin1, J7.pin1, J8.pin1, J9.pin1, J10.pin1, J11.pin1, J12.pin1, J13.pin1, J14.pin1, J15.pin1, J17.pin1, J18.GNDBREAK
  N2: J5.pin2, J6.pin2, J7.pin2, J8.pin2, J9.pin2, J10.pin2, J11.pin2, J12.pin2, J13.pin2, J14.pin2, J15.pin2, J17.pin2, J18.PWR
  N3: J5.pin3, J16.pin1
  N4: J6.pin3, J16.pin2
  N5: J7.pin3, J16.pin3
  N6: J8.pin3, J16.pin4
  N7: J9.pin3, J16.pin5
  N8: J10.pin3, J16.pin6
  N9: J11.pin3, J16.pin7
  N10: J12.pin3, J16.pin8
  N11: J13.pin3, J16.pin9
  N12: J14.pin3, J16.pin10
  N13: J15.pin3, J16.pin11
  N14: J16.pin12, J18.GND
  N15: J19.pin1, J20.pin1, J21.pin1, J22.pin1, J23.pin1, J25.pin1, J26.pin1, J27.pin1, J28.pin1, J29.pin1, J30.pin1, J31.pin1, J32.GNDBREAK
  N16: J19.pin2, J20.pin2, J21.pin2, J22.pin2, J23.pin2, J25.pin2, J26.pin2, J27.pin2, J28.pin2, J29.pin2, J30.pin2, J31.pin2, J32.PWR
  N17: J19.pin3, J24.pin6
  N18: J20.pin3, J24.pin2
  N19: J21.pin3, J24.pin3
  N20: J23.pin3, J24.pin8
  N21: J24.pin1, J27.pin3
  N22: J24.pin4, J31.pin3
  N23: J24.pin5, J30.pin3
  N24: J24.pin7, J26.pin3
  N25: J24.pin9, J28.pin3
  N26: J24.pin10, J25.pin3
  N27: J24.pin11, J29.pin3
  N28: J24.pin12, J32.GND
  N29: J33.pin1, J34.pin1, J35.pin1, J36.pin1, J37.pin1, J39.pin1, J40.pin1, J41.pin1, J42.pin1, J43.pin1, J44.pin1, J45.pin1, J46.GNDBREAK
  N30: J33.pin2, J34.pin2, J35.pin2, J36.pin2, J37.pin2, J39.pin2, J40.pin2, J41.pin2, J42.pin2, J43.pin2, J44.pin2, J45.pin2, J46.PWR
  N31: J33.pin3, J38.pin6
  N32: J34.pin3, J38.pin2
  N33: J35.pin3, J38.pin3
  N34: J37.pin3, J38.pin8
  N35: J38.pin1, J41.pin3
  N36: J38.pin4, J45.pin3
  N37: J38.pin5, J44.pin3
  N38: J38.pin7, J40.pin3
  N39: J38.pin9, J42.pin3
  N40: J38.pin10, J39.pin3
  N41: J38.pin11, J43.pin3
  N42: J38.pin12, J46.GND
  N43: J47.pin1, J48.pin1, J49.pin1, J50.pin1, J51.pin1, J53.pin1, J54.pin1, J55.pin1, J56.pin1, J57.pin1, J58.pin1, J59.pin1, J60.GNDBREAK
  N44: J47.pin2, J48.pin2, J49.pin2, J50.pin2, J51.pin2, J53.pin2, J54.pin2, J55.pin2, J56.pin2, J57.pin2, J58.pin2, J59.pin2, J60.PWR
  N45: J47.pin3, J52.pin6
  N46: J48.pin3, J52.pin2
  N47: J49.pin3, J52.pin3
  N48: J51.pin3, J52.pin8
  N49: J52.pin1, J55.pin3
  N50: J52.pin4, J59.pin3
  N51: J52.pin5, J58.pin3
  N52: J52.pin7, J54.pin3
  N53: J52.pin9, J56.pin3
  N54: J52.pin10, J53.pin3
  N55: J52.pin11, J57.pin3
  N56: J52.pin12, J60.GND
