# Fritzing sketch ERP_RemoteControl (saved by Fritzing 0.8.7b)
breadboards: 1

parts:
  Part1 = Arduino Uno (Rev3)
  Part2 = Thumb Joystick
  VCC1 = Battery block 9V  # not connected

nets:
  N1: Part1.A4/SDA, Part2.HORZ
  N2: Part1.A5/SCL, Part2.VERT
  5V: Part1.5V, Part2.VCC
  GND: Part1.GND, Part2.GND
