# Fritzing sketch ERP_Remote_Controller_ProMini_3V3 (saved by Fritzing 0.8.7b)
circuit board: 8.46667cm x 5.64444cm
breadboards: 1

parts:
  J4 = female pin header, 3 pins [form="♀ (female)"]
  J5 = female pin header, 3 pins [form="♀ (female)"]
  Part1 = Arduino Pro Mini v13
  J6 = double row female pin header, 8 pins [form="♀ (female)"]  # not connected
  Power_plug1 = Power plug

nets:
  N1: J4.pin1, J5.pin3, Part1.GND
  N2: J4.pin3, J5.pin1, Part1.VCC
  N3: Part1.DTR, Power_plug1.GND
  N4: Part1.RAW, Power_plug1.VCC
