# Fritzing sketch LM317_Voltage_Regulator (saved by Fritzing 0.8.3b)
circuit board: 5.21168cm x 3.34197cm
breadboards: 1

parts:
  U1 = Voltage Regulator - Variable [package="TO220 [THT]"]
  R1 = Resistor [tolerance=±5% resistance=10k package=THT]
  J1 = female pin header, 1 pin [form="♀ (female)"]
  J3 = female pin header, 1 pin [form="♀ (female)"]
  J4 = female pin header, 4 pins [form="♀ (female)"]
  R2 = Resistor [tolerance=±5% resistance=1k package=THT]
  R3 = Resistor [tolerance=±5% resistance=2.2k package=THT]
  R4 = Resistor [tolerance=±5% resistance=3.3k package=THT]
  R5 = Resistor [tolerance=±5% resistance=1.5k package=THT]
  R6 = Resistor [tolerance=±5% resistance=100 package=THT]
  R7 = Resistor [tolerance=±5% resistance=100 package=THT]
  R8 = Resistor [tolerance=±5% resistance=330 package=THT]
  J2 = female pin header, 2 pins [form="♀ (female)"]
  J6 = Power Jack [package=power_jack_pth]
  C1 = Electrolytic Capacitor [capacitance=0.1µF package="0405 [SMD, electrolytic]"]
  C2 = Electrolytic Capacitor [capacitance=1µF package="0405 [SMD, electrolytic]"]

nets:
  N1: U1.ADJ, R1.Pin_1, R4.Pin_0, R6.Pin_1, R7.Pin_1, R8.Pin_0
  N2: U1.OUT, J1.pin1, J3.pin1, C2.+
  N3: U1.IN, J6.PWR, C1.+
  GND: R1.Pin_0, J2.pin1, J2.pin2, J6.GNDBREAK, C1.-, C2.-
  N4: J4.pin1, R2.Pin_1
  N5: J4.pin2, R5.Pin_1
  N6: J4.pin3, R3.Pin_1
  N7: J4.pin4, R4.Pin_1
  N8: R2.Pin_0, R6.Pin_0
  N9: R3.Pin_0, R8.Pin_1
  N10: R5.Pin_0, R7.Pin_0
