# Fritzing sketch ML-L3_Remote (saved by Fritzing 0.8.7b)
breadboards: 1

parts:
  S1 = Pushbutton [package="[THT]"]
  R2 = Resistor [tolerance=±5% resistance=10k package=THT]
  R3 = Resistor [tolerance=±5% resistance=2.2k package=THT]
  R4 = Resistor [tolerance=±5% resistance=4.7k package=THT]
  R5 = Resistor [tolerance=±5% resistance=6.8k package=THT]
  R6 = Resistor [tolerance=±5% resistance=10k package=THT]
  J1 = female pin header, 2 pins [form="♀ (female)"]
  J2 = female pin header, 2 pins [form="♀ (female)"]
  J3 = female pin header, 2 pins [form="♀ (female)"]
  LED3 = LED - 5mm [color="Red (633nm)" package="5 mm [THT]"]
  R16 = Resistor [tolerance=±5% resistance=220 package=THT]
  LED4 = LED - 5mm [color="Red (633nm)" package="5 mm [THT]"]
  R17 = Resistor [tolerance=±5% resistance=220 package=THT]
  LED5 = LED - 5mm [color="Red (633nm)" package="5 mm [THT]"]
  R18 = Resistor [tolerance=±5% resistance=220 package=THT]
  LED6 = LED - 5mm [color="Red (633nm)" package="5 mm [THT]"]
  R19 = Resistor [tolerance=±5% resistance=220 package=THT]
  R20 = Resistor [tolerance=±5% resistance=10k package=THT]
  R21 = Resistor [tolerance=±5% resistance=6.8k package=THT]
  R22 = Photocell (LDR) [package=THT]
  LED7 = LED - 5mm [color="Red (633nm)" package="5 mm [THT]"]
  R23 = Resistor [tolerance=±5% resistance=220 package=THT]
  LED8 = LED - 5mm [color="Red (633nm)" package="5 mm [THT]"]
  R24 = Resistor [tolerance=±5% resistance=220 package=THT]
  U1 = mystery part, 3 pins [chip_label=?]
  U2 = mystery part, 3 pins [chip_label=?]
  U3 = mystery part, 3 pins [chip_label=?]
  R25 = Resistor [tolerance=±5% resistance=220 package=THT]
  S2 = Pushbutton [package="[THT]"]
  R26 = Resistor [tolerance=±5% resistance=10k package=THT]
  S3 = Toggle Switch [package=THT]
  R27 = Resistor [tolerance=±5% resistance=10k package=THT]
  Part1 = Arduino Pro Mini v13

nets:
  N1: S1.Pin_1, S1.Pin_2, R2.Pin_1, R21.Pin_1, U1.pin3, U2.pin2, U3.pin2, R25.Pin_1, S2.Pin_3, S2.Pin_4, R26.Pin_1, S3.L1, Part1.VCC, Part1.D4
  N2: S1.Pin_3, S1.Pin_4, R20.Pin_0, Part1.D2
  N3: R2.Pin_0, R3.Pin_1, R4.Pin_1, R5.Pin_1, R6.Pin_1, Part1.A0
  N4: R3.Pin_0, J1.pin1
  N5: R4.Pin_0, J1.pin2
  N6: R5.Pin_0, J2.pin1
  N7: R6.Pin_0, J2.pin2
  N8: J3.pin1, J3.pin2, R16.Pin_0, R17.Pin_0, R18.Pin_0, R19.Pin_0, R20.Pin_1, R22.pin_0, R23.Pin_0, R24.Pin_0, U1.pin1, U2.pin1, U3.pin3, R25.Pin_0, Part1.GND
  N9: LED3.cathode, Part1.D8
  N10: LED3.anode, R16.Pin_1
  N11: LED4.cathode, Part1.D7
  N12: LED4.anode, R17.Pin_1
  N13: LED5.cathode, Part1.D6_PWM
  N14: LED5.anode, R18.Pin_1
  N15: LED6.cathode, Part1.D5_PWM
  N16: LED6.anode, R19.Pin_1
  N17: R21.Pin_0, R22.pin_1, Part1.A1
  N18: LED7.cathode, Part1.D3_PWM
  N19: LED7.anode, R23.Pin_1
  N20: LED8.cathode, Part1.D0/TX
  N21: LED8.anode, R24.Pin_1
  N22: U1.pin2, Part1.D10_PWM/SS
  N23: U2.pin3, Part1.A3
  N24: U3.pin1, Part1.A2
  N25: S2.Pin_1, S2.Pin_2, Part1.D9_PWM
  N26: S3.COM, R27.Pin_1
  N27: R27.Pin_0, Part1.D11_PWM/MOSI
