# Fritzing sketch ML_L3_Remote_With_LCD (saved by Fritzing 0.8.7b)
breadboards: 1

parts:
  Part1 = Arduino Pro Mini v13
  R1 = Rotary Potentiometer (Small) [maximum_resistance=100kΩ package=THT]  # not connected
  J2 = female pin header, 16 pins [form="♀ (female)"]
  J3 = female pin header, 2 pins [form="♀ (female)"]
  J4 = female pin header, 3 pins [form="♀ (female)"]
  U1 = LCD-16X2 [package=lcd-16x2]  # not connected
  R2 = Resistor [tolerance=±5% resistance=100k package=THT]
  R3 = Resistor [tolerance=±5% resistance=46k package=THT]
  R4 = Resistor [tolerance=±5% resistance=100k package=THT]
  R5 = Resistor [tolerance=±5% resistance=330k package=THT]
  R6 = Resistor [tolerance=±5% resistance=520k package=THT]
  J5 = female pin header, 4 pins [form="♀ (female)"]
  J6 = female pin header, 1 pin [form="♀ (female)"]
  S1 = Square Pushbutton  # not connected
  R7 = Rotary Potentiometer (Small) [maximum_resistance=100kΩ package=THT]
  R8 = Rotary Potentiometer (Small) [maximum_resistance=100kΩ package=THT]
  R9 = Resistor [tolerance=±5% resistance=4.7k package=THT]
  R10 = Photocell (LDR) [package=THT]
  LED1 = LED - 5mm [color="Red (633nm)" package="5 mm [THT]"]
  LED2 = LED - 5mm [color="Red (633nm)" package="5 mm [THT]"]
  S2 = Pushbutton [package="[THT]"]
  R11 = Resistor [tolerance=±5% resistance=100k package=THT]
  R12 = Resistor [tolerance=±5% resistance=100k package=THT]
  S3 = Pushbutton [package="[THT]"]
  J7 = female pin header, 1 pin [form="♀ (female)"]
  J8 = female pin header, 1 pin [form="♀ (female)"]
  J9 = female pin header, 1 pin [form="♀ (female)"]
  J10 = female pin header, 1 pin [form="♀ (female)"]
  J11 = female pin header, 3 pins [form="♀ (female)"]
  J12 = female pin header, 3 pins [form="♀ (female)"]
  J13 = female pin header, 2 pins [form="♀ (female)"]
  J14 = female pin header, 2 pins [form="♀ (female)"]
  VCC1 = Battery block 9V
  J15 = female pin header, 2 pins [form="♀ (female)"]
  U2 = SWITCH-SPST-2 [package=switch-spst-vertical]
  R13 = Resistor [tolerance=±5% resistance=220 package=THT]
  R14 = Resistor [tolerance=±5% resistance=220 package=THT]
  R15 = Resistor [tolerance=±5% resistance=520k package=THT]
  R16 = Resistor [tolerance=±5% resistance=46k package=THT]
  R17 = Resistor [tolerance=±5% resistance=100k package=THT]
  J16 = female pin header, 1 pin [form="♀ (female)"]
  J17 = female pin header, 1 pin [form="♀ (female)"]
  J18 = female pin header, 1 pin [form="♀ (female)"]
  J19 = female pin header, 3 pins [form="♀ (female)"]

nets:
  N1: Part1.GND, J2.pin1, J2.pin5, J2.pin16, J4.pin3, R3.Pin_0, R4.Pin_0, R5.Pin_0, R6.Pin_0, R7.leg2, R8.leg2, R10.pin_0, R11.Pin_1, R12.Pin_1, J11.pin3, J12.pin3, VCC1.-, R13.Pin_0, R14.Pin_0, R15.Pin_0, R16.Pin_0, J19.pin3
  N2: Part1.A4, R17.Pin_0, J16.pin1
  N3: Part1.RAW, J15.pin2, U2.P
  N4: Part1.VCC, J2.pin2, J3.pin1, J4.pin1, R2.Pin_1, R7.leg1, R8.leg1, R9.Pin_1, S2.Pin_3, S2.Pin_4, S3.Pin_3, S3.Pin_4, J7.pin1, J9.pin1, J11.pin1, J12.pin1, R17.Pin_1
  N5: Part1.A3, R2.Pin_0, J6.pin1
  N6: Part1.A2, R9.Pin_0, R10.pin_1
  N7: Part1.A1, R7.wiper, J11.pin2
  N8: Part1.A0, R8.wiper, J12.pin2
  N9: Part1.D13/SCK, J19.pin1
  N10: Part1.D12/MISO, R12.Pin_0, S3.Pin_1, S3.Pin_2, J8.pin1
  N11: Part1.D11_PWM/MOSI, J19.pin2
  N12: Part1.D10_PWM/SS, J2.pin4
  N13: Part1.D9_PWM, LED1.anode, J13.pin2
  N14: Part1.D8, LED2.anode, J14.pin2
  N15: Part1.D7, J2.pin14
  N16: Part1.D6_PWM, J2.pin13
  N17: Part1.D5_PWM, J2.pin12
  N18: Part1.D4, J2.pin11
  N19: Part1.D3_PWM, J2.pin6
  N20: Part1.D2, S2.Pin_1, S2.Pin_2, R11.Pin_0, J10.pin1
  N21: J2.pin3, J4.pin2
  N22: J2.pin15, J3.pin2
  N23: R3.Pin_1, J5.pin1
  N24: R4.Pin_1, J5.pin2
  N25: R5.Pin_1, J5.pin3
  N26: R6.Pin_1, J5.pin4
  N27: LED1.cathode, J13.pin1, R14.Pin_1
  N28: LED2.cathode, J14.pin1, R13.Pin_1
  N29: VCC1.+, J15.pin1, U2.O
  N30: R15.Pin_1, J18.pin1
  N31: R16.Pin_1, J17.pin1
