# Fritzing sketch ML_L3_Remote_With_LCD_PCB_Version (saved by Fritzing 0.8.7b)
circuit board: 9.0903cm x 7.55339cm
breadboards: 1

parts:
  Part1 = Arduino Pro Mini v13
  J3 = female pin header, 2 pins [form="♀ (female)"]
  J4 = female pin header, 3 pins [form="♀ (female)"]
  R2 = Resistor [tolerance=±5% resistance=100k package=THT]
  R3 = Resistor [tolerance=±5% resistance=46k package=THT]
  R4 = Resistor [tolerance=±5% resistance=100k package=THT]
  R5 = Resistor [tolerance=±5% resistance=330k package=THT]
  R6 = Resistor [tolerance=±5% resistance=520k package=THT]
  J5 = female pin header, 4 pins [form="♀ (female)"]
  J6 = female pin header, 1 pin [form="♀ (female)"]
  R9 = Resistor [tolerance=±5% resistance=4.7k package=THT]
  R10 = Photocell (LDR) [package=THT]
  R11 = Resistor [tolerance=±5% resistance=100k package=THT]
  R12 = Resistor [tolerance=±5% resistance=100k package=THT]
  J7 = female pin header, 1 pin [form="♀ (female)"]
  J8 = female pin header, 1 pin [form="♀ (female)"]
  J9 = female pin header, 1 pin [form="♀ (female)"]
  J14 = female pin header, 2 pins [form="♀ (female)"]
  J15 = female pin header, 2 pins [form="♀ (female)"]
  J16 = female pin header, 2 pins [form="♀ (female)"]
  J17 = female pin header, 6 pins [form="♀ (female)"]
  J18 = female pin header, 6 pins [form="♀ (female)"]
  J19 = female pin header, 2 pins [form="♀ (female)"]
  J13 = female pin header, 2 pins [form="♀ (female)"]
  J2 = female pin header, 16 pins [form="♀ (female)"]
  J11 = female pin header, 3 pins [form="♀ (female)"]
  R13 = Resistor [tolerance=±5% resistance=220 package=THT]
  R14 = Resistor [tolerance=±5% resistance=220 package=THT]
  J20 = female pin header, 1 pin [form="♀ (female)"]
  J23 = female pin header, 1 pin [form="♀ (female)"]
  J24 = female pin header, 1 pin [form="♀ (female)"]
  R15 = Resistor [tolerance=±5% resistance=100k package=THT]
  R16 = Resistor [tolerance=±5% resistance=46k package=THT]
  R17 = Resistor [tolerance=±5% resistance=520k package=THT]
  J25 = female pin header, 1 pin [form="♀ (female)"]
  J26 = female pin header, 1 pin [form="♀ (female)"]
  J27 = female pin header, 1 pin [form="♀ (female)"]
  J28 = female pin header, 1 pin [form="♀ (female)"]
  J29 = female pin header, 1 pin [form="♀ (female)"]
  J30 = female pin header, 1 pin [form="♀ (female)"]
  J31 = female pin header, 3 pins [form="♀ (female)"]
  J32 = female pin header, 3 pins [form="♀ (female)"]
  J10 = female pin header, 2 pins [form="♀ (female)"]

nets (from the pcb view):
  N1: Part1.DTR, J17.pin6
  N2: Part1.D0/TX, J17.pin5
  N3: Part1.D1/RX, J3.pin1, J4.pin1, J9.pin1, J17.pin4, J2.pin2
  N4: Part1.VCC, R2.Pin_1, R9.Pin_1, J7.pin1, J17.pin3, J11.pin1, R15.Pin_1, J31.pin1
  N5: Part1.GND, J4.pin3, R3.Pin_0, R4.Pin_0, R5.Pin_0, R6.Pin_0, R10.pin_0, R11.Pin_1, R12.Pin_1, J16.pin1, J17.pin1, J17.pin2, J2.pin1, J2.pin5, J2.pin16, J11.pin3, R13.Pin_0, R14.Pin_0, R16.Pin_0, R17.Pin_0, J31.pin3, J32.pin3
  N6: Part1.A4, R15.Pin_0, J25.pin1
  N7: Part1.RAW, J15.pin2
  N8: Part1.A3, J18.pin6
  N9: Part1.A2, J18.pin5
  N10: Part1.A1, J18.pin4
  N11: Part1.A0, J18.pin3
  N12: Part1.D13/SCK, J18.pin2, J32.pin1
  N13: Part1.D12/MISO, R12.Pin_0, J8.pin1, J18.pin1
  N14: Part1.D11_PWM/MOSI, J32.pin2
  N15: Part1.D10_PWM/SS, J29.pin1
  N16: Part1.D9_PWM, J19.pin2
  N17: Part1.D8, J19.pin1
  N18: Part1.D7, J2.pin14
  N19: Part1.D6_PWM, J2.pin13
  N20: Part1.D5_PWM, J2.pin12
  N21: Part1.D4, J2.pin11
  N22: Part1.D3_PWM, J2.pin6
  N23: Part1.D2, J28.pin1
  N24: J3.pin2, J2.pin15
  N25: J4.pin2, J2.pin3
  N26: R2.Pin_0, J6.pin1
  N27: R3.Pin_1, J5.pin1
  N28: R4.Pin_1, J5.pin2
  N29: R5.Pin_1, J5.pin3
  N30: R6.Pin_1, J5.pin4
  N31: R9.Pin_0, R10.pin_1, J20.pin1
  N32: R11.Pin_0, J10.pin1, J10.pin2
  N33: J14.pin1, R13.Pin_1
  N34: J14.pin2, J23.pin1
  N35: J15.pin1, J16.pin2
  N36: J13.pin1, R14.Pin_1
  N37: J13.pin2, J24.pin1
  N38: J2.pin4, J30.pin1
  N39: R16.Pin_1, J26.pin1
  N40: R17.Pin_1, J27.pin1

notes:
  Designed by vu2aeo
  Multi-Functional IR
  DSLR Remote Control
