# Fritzing sketch Ten _Servo_Controller (saved by Fritzing 0.8.3b)
circuit board: 6.12397cm x 2.772cm
breadboards: 1

parts:
  J3 = female pin header, 3 pins [form="♀ (female)"]
  J4 = female pin header, 3 pins [form="♀ (female)"]
  J5 = female pin header, 3 pins [form="♀ (female)"]
  J6 = female pin header, 3 pins [form="♀ (female)"]
  J7 = female pin header, 3 pins [form="♀ (female)"]
  J8 = female pin header, 3 pins [form="♀ (female)"]
  J9 = female pin header, 3 pins [form="♀ (female)"]
  J11 = Power Jack [package=power_jack_pth]
  J12 = female pin header, 1 pin [form="♀ (female)"]
  JP1 = Header 5x2 [package=2x5-ra]
  J2 = female pin header, 3 pins [form="♀ (female)"]
  J13 = female pin header, 1 pin [form="♀ (female)"]

nets:
  N1: J3.pin1, J4.pin1, J5.pin1, J6.pin1, J7.pin1, J8.pin1, J9.pin1, J11.GND, J11.GNDBREAK, J12.pin1, JP1.9, J2.pin1
  N2: J3.pin2, J4.pin2, J5.pin2, J6.pin2, J7.pin2, J8.pin2, J9.pin2, J11.PWR, JP1.7, J2.pin2, J13.pin1
  N3: J3.pin3, JP1.8
  N4: J4.pin3, JP1.6
  N5: J5.pin3, JP1.4
  N6: J6.pin3, JP1.2
  N7: J7.pin3, JP1.1
  N8: J8.pin3, JP1.3
  N9: J9.pin3, JP1.5
  N10: JP1.10, J2.pin3
