# Fritzing sketch Two-Pot-Meter (saved by Fritzing 0.8.7b)
breadboards: 1

parts:
  R1 = Rotary Potentiometer (Small) [maximum_resistance=100kΩ package=THT]
  R2 = Rotary Potentiometer (Small) [maximum_resistance=100kΩ package=THT]
  Part1 = Arduino Uno (Rev3)

nets:
  N1: R1.leg1, R2.leg1, Part1.5V
  N2: R1.wiper, Part1.A1
  N3: R1.leg2, R2.leg2, Part1.GND
  N4: R2.wiper, Part1.A0
