# Fritzing sketch _3DOF_Haptic_Control (saved by Fritzing 0.8.3b)
breadboards: 2

parts:
  Part1 = Arduino Uno (Rev3)
  R1 = Resistor [tolerance=±5% resistance=6.8k package=THT]
  Part2 = Triple Axis Accelerometer Breakout - ADXL345
  R2 = Resistor [tolerance=±5% resistance=6.8k package=THT]
  R4 = Resistor [tolerance=±5% resistance=47k package=THT]
  J1 = Basic Servo
  J2 = Basic Servo
  J3 = Basic Servo
  VCC1 = 4 x AAA Battery Mount
  R3 = Basic Flex Resistor

nets:
  N1: Part1.A1, R3.pin_1
  N2: Part1.ICSP_MOSI, Part1.D11_PWM/MOSI, J1.pulse
  GND: Part1.GND, Part2.GND, J1.gnd, J2.gnd, J3.gnd, VCC1.-, R3.Pin_2
  N3: Part1.D9_PWM, J3.pulse
  N4: Part1.D10_PWM/SS, J2.pulse
  3V3: Part1.3V3, R1.Pin_1, Part2.VCC, Part2.CS, Part2.SDO, R2.Pin_1
  N5: Part1.5V, R4.Pin_1
  N6: R1.Pin_0, Part2.SCL
  N7: Part2.SDA, R2.Pin_0
  VCC: J1.vcc, J2.vcc, J3.vcc, VCC1.+
