# Fritzing sketch mpu_6050 (saved by Fritzing 0.8.3b)
breadboards: 1

parts:
  R1 = Resistor [tolerance=±5% resistance=6.8k package=THT]
  R2 = Resistor [tolerance=±5% resistance=6.8k package=THT]
  Part1 = Arduino Uno (Rev3)
  Part2 = IMU Digital Combo Board 6DOF

nets:
  N1: R1.Pin_0, Part1.A4/SDA, Part2.SDA
  3V3: R1.Pin_1, R2.Pin_1, Part1.3V3, Part2.3.3V
  N2: R2.Pin_0, Part1.A5/SCL, Part2.SCL
