# Fritzing sketch pro_mini_6_Servo_controller (saved by Fritzing 0.8.3b)
circuit board: 8.5593cm x 5.44621cm
breadboards: 1

parts:
  Part1 = Arduino Pro Mini 3.3V
  J1 = female pin header, 2 pins [form="♀ (female)"]
  J2 = female pin header, 2 pins [form="♀ (female)"]
  J3 = female pin header, 4 pins [form="♀ (female)"]
  J4 = female pin header, 12 pins [form="♀ (female)"]
  J5 = female pin header, 12 pins [form="♀ (female)"]
  J6 = female pin header, 4 pins [form="♀ (female)"]
  J7 = female pin header, 4 pins [form="♀ (female)"]
  J8 = female pin header, 6 pins [form="♀ (female)"]
  J9 = Power Jack [package=power_jack_pth_lock]
  J10 = female pin header, 3 pins [form="♀ (female)"]
  J11 = female pin header, 3 pins [form="♀ (female)"]
  J12 = female pin header, 3 pins [form="♀ (female)"]
  J13 = female pin header, 3 pins [form="♀ (female)"]
  J14 = female pin header, 3 pins [form="♀ (female)"]
  J15 = female pin header, 3 pins [form="♀ (female)"]
  J16 = female pin header, 3 pins [form="♀ (female)"]
  J17 = female pin header, 3 pins [form="♀ (female)"]

nets:
  N1: Part1.DTR, J8.pin1
  N2: Part1.TXO, J4.pin12, J8.pin2
  N3: Part1.RXI, J4.pin11, J8.pin3
  N4: Part1.VCC, J8.pin4
  GND: Part1.GND, J5.pin11, J8.pin5, J8.pin6, J9.GND, J9.GNDBREAK, J10.pin1, J11.pin1, J12.pin1, J13.pin1, J14.pin1, J15.pin1, J16.pin1, J17.pin1
  N5: Part1.A4, J4.pin9
  N6: Part1.A5, J5.pin9
  N7: Part1.RAW, J5.pin12, J9.PWR, J10.pin2, J11.pin2, J12.pin2, J13.pin2, J14.pin2, J15.pin2, J16.pin2, J17.pin2
  N8: Part1.RESET, J4.pin10, J5.pin10
  N9: Part1.A3, J5.pin8
  N10: Part1.A2, J5.pin7
  N11: Part1.A1, J5.pin6
  N12: Part1.A0, J5.pin5
  N13: Part1.SCK, J5.pin4
  N14: Part1.MISO, J5.pin3
  N15: Part1.MOSI, J5.pin2, J14.pin3
  N16: Part1.D10, J5.pin1, J15.pin3
  N17: Part1.D9, J4.pin1, J13.pin3
  N18: Part1.D8, J4.pin2
  N19: Part1.D7, J4.pin3
  N20: Part1.D6, J4.pin4, J12.pin3
  N21: Part1.D5, J4.pin5, J11.pin3
  N22: Part1.D4, J4.pin6
  N23: Part1.D3, J4.pin7, J10.pin3
  N24: Part1.D2, J4.pin8
  N25: J1.pin1, J3.pin3
  N26: J1.pin2, J3.pin4
  N27: J2.pin1, J3.pin1, J7.pin1, J7.pin2, J7.pin3, J7.pin4
  N28: J2.pin2, J3.pin2, J6.pin1, J6.pin2, J6.pin3, J6.pin4
