# Fritzing sketch rover-design1 (saved by Fritzing 0.8.3b)
breadboards: 1

parts:
  M1 = DC Motor
  M2 = DC Motor
  M3 = DC Motor
  M4 = DC Motor
  IC1 = L293D [package=THT]
  Part1 = Arduino Uno (Rev3)
  BAT1 = BC9VPC [package=bc9vpc]
  Part2 = 9 Degrees of Freedom - Sensor Stick
  J1 = Infrared Proximity Sensor

nets:
  N1: M1.pin_1, M4.pin_1, IC1.Out_2_(_Controlled_by_Enable_1_)
  N2: M1.pin_2, M4.pin_2, IC1.Out_1_(_Controlled_by_Enable_1_)
  N3: M2.pin_1, M3.pin_1, IC1.Out_4_(_Controlled_by_Enable_2_)
  N4: M2.pin_2, M3.pin_2, IC1.Out_3_(_Controlled_by_Enable_2_)
  N5: IC1.Enable_1, Part1.D3_PWM
  N6: IC1.In_1, Part1.D2
  GND: IC1.0V, Part1.GND, BAT1.V-, Part2.GND, J1.GND
  N7: IC1.In_2, Part1.D4
  N8: IC1.Enable_2, Part1.D11_PWM/MOSI
  N9: IC1.In_3, Part1.D12/MISO
  N10: IC1.In_4, Part1.D10_PWM/SS
  N11: IC1.+V, Part1.VIN, BAT1.V+
  N12: Part1.A0, J1.Vout
  N13: Part1.A4/SDA, Part2.SDA
  N14: Part1.A5/SCL, Part2.SCL
  5V: Part1.5V, J1.Vcc
  3V3: Part1.3V3, Part2.VCC
